# Fritzing sketch TemperatureSensor (saved by Fritzing 0.9.2b)
breadboards: 1

parts:
  Composant1 = Arduino Uno (Rev3)
  T1 = TMP36 Temperature Sensor [thermistor_type=NTC package="TO92 [THT]"]
  R1 = Resistor [tolerance=±5% resistance=4.7k package=THT]
  LCD1 = LCD screen
  R2 = Trimmer Potentiometer [maximum_resistance=10kΩ package=THT]
  S1 = Pushbutton [package="[THT]"]
  R3 = Resistor [tolerance=±5% resistance=10k package=THT]
  U1 = ESP8266 WiFi Module [part_number=ESP8266]

nets:
  N1: Composant1.D9_PWM, U1.TXD
  N2: Composant1.D10_PWM/SS, U1.RXD
  N3: Composant1.D11_PWM/MOSI, LCD1.E
  N4: Composant1.D12/MISO, LCD1.RS
  N5: Composant1.D2, T1.Vout, R1.Pin_0
  N6: Composant1.D3_PWM, LCD1.DB7
  N7: Composant1.D4, LCD1.DB6
  N8: Composant1.D5_PWM, LCD1.DB5
  N9: Composant1.D6_PWM, LCD1.DB4
  N10: Composant1.D7, S1.Pin_3, S1.Pin_4
  3V3: Composant1.3V3, U1.VCC, U1.CH_PD
  5V: Composant1.5V, T1.+Vs, R1.Pin_1, LCD1.VDD, R2.leg1, S1.Pin_1, S1.Pin_2, R3.Pin_1
  GND: Composant1.GND, T1.GND, LCD1.VSS, LCD1.R/W, LCD1.LED-, R2.leg2, U1.GND
  N11: LCD1.V0, R2.wiper
  N12: LCD1.LED+, R3.Pin_0

custom parts:
  ESP8266 WiFi Module: Generic WiFi Module based on the ESP8266 with onboard PCB antenna and UART communications
